# Fritzing sketch Data Acquistion (saved by Fritzing 0.9.3b)
breadboards: 1

parts:
  R1 = Resistor [tolerance=±5% resistance=10k package=THT]  # not connected
  Part1 = Adafruit Feather M0 Adalogger [part_number="Adafruit #2796"]
  J1 = Basic Force Sensing Resistor (FSR) [package=THT]  # not connected
  Part2 = Adafruit LSM9DS1 9DoF Breakout [part_number="Adafruit #3387"]

nets:
  GND: Part1.GND, Part1.D11, Part1.D9, Part2.GND
  N1: Part1.MISO, Part1.+3V3, Part2.INT2_AG
  N2: Part1.A1, Part2.DEN
  N3: Part1.AREF, Part1.SCL, Part2.VIN
  N4: Part1.D10, Part2.CS_MAG
  N5: Part1.SDA, Part2.INT1_AG
  N6: Part2.SDO_M, Part2.SDO_AG

custom parts:
  Adafruit Feather M0 Adalogger: This is the Adafruit Feather M0 Adalogger - our take on an 'all-in-one' Cortex M0 datalogger (or data-reader) with built in USB and battery charging. Its an Adafruit Feather M0 with a microSD holder ready to rock! We have other boards in the Feather family, check'em out here At the Feather M0's heart is an ATSAMD21G18 ARM Cortex M0 processor, clocked at 48 MHz and at 3.3V logic, the same one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
  Adafruit LSM9DS1 9DoF Breakout: Add motion, direction and orientation sensing to your Arduino project with this all-in-one 9-DOF sensor. Inside the chip are three sensors, one is a classic 3-axis accelerometer, which can tell you which direction is down towards the Earth (by measuring gravity) or how fast the board is accelerating in 3D space. The other is a 3-axis magnetometer that can sense where the strongest magnetic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
